# Fritzing sketch Astable Flip-Flop Circuit 2023-12-06 (saved by Fritzing 1.0.0rc)
circuit board: 5.5cm x 5.5cm
breadboards: 1

parts:
  R1 = Resistor [tolerance=±5% resistance=470 power=0.25W package=THT]
  R2 = Resistor [tolerance=±5% resistance=470 power=0.25W mn=470 package=THT]
  LED1 = LED - 5mm [color="Red (633nm)" current=30mA package="5 mm [THT]"]
  LED2 = LED - 5mm [color="Green (570nm)" current=0.030A package="5 mm [THT]"]
  R3 = Resistor [tolerance=±5% resistance=100k power=0.25W mn=or10kΩ package=THT]
  R4 = Resistor [tolerance=±5% resistance=100k power=0.25W mn=(=R3) package=THT]
  Q1 = NPN-Transistor [package="TO92 [THT]"]
  Q2 = NPN-Transistor [package="TO92 [THT]"]
  J1 = male pin header, 1 pin [form="♂ (male)"]
  J2 = male pin header, 1 pin [form="♂ (male)"]
  C1 = Ceramic Capacitor [capacitance=10µF voltage=35V mn="or 1µF" package="200 mil [THT, multilayer]"]
  C2 = Ceramic Capacitor [capacitance=10µF voltage=35V mn=(=C1) package="200 mil [THT, multilayer]"]
  +9V = Screw terminal - 2 pins [package=THT]
  J3 = male pin header, 1 pin [form="♂ (male)"]

nets:
  N1: R1.Pin_0, R2.Pin_0, R3.Pin_0, R4.Pin_0, +9V.pin1
  N2: R1.Pin_1, LED1.anode
  N3: R2.Pin_1, LED2.anode
  N4: LED1.cathode, Q1.C, J1.pin1, C1.1
  N5: LED2.cathode, Q2.C, J2.pin1, C2.1
  N6: R3.Pin_1, Q2.B, C1.0
  N7: R4.Pin_1, Q1.B, C2.0
  N8: Q1.E, Q2.E, +9V.pin2, J3.pin1

notes:
  R 100k x C 10µF =1.0s
  Flip-Flop
  R  10k x C 10µF =0.1s
  R 100k x C  1µF =0.1s
  GND
  BC547
  E
  C
  B
  Ver. 2023.11.17
  Blink time T = R x C
  by DM9GP
  -
  +
